# Fritzing sketch circuit_diagram (saved by Fritzing 0.9.3b)
breadboards: 1

parts:
  Part1 = Arduino Uno (Rev3)
  J1 = Basic Servo
  J2 = Basic Servo
  J3 = Basic Servo
  J5 = Basic Servo
  M1 = LJ18A3-H-ZBX [package=THT]
  SD_card_module1 = SD Card Module
  BAT1 = BC9VPC [package=bc9vpc]
  J6 = Basic Servo
  J7 = Basic Servo
  U1 = LIPO-2000mAh [package=lipo-2000]

nets:
  N1: Part1.D8, J1.pulse
  N2: Part1.D9_PWM, J2.pulse
  N3: Part1.D10_PWM/SS, SD_card_module1.CS
  N4: Part1.D11_PWM/MOSI, SD_card_module1.MOSI
  N5: Part1.D12/MISO, SD_card_module1.MISO
  N6: Part1.D13/SCK, SD_card_module1.SCK
  GND: Part1.GND, J1.gnd, J3.gnd, M1.SIG_(BLK), BAT1.V-, U1.-
  N7: Part1.AREF, SD_card_module1.GND
  N8: Part1.D2, M1.VI_(BRN)
  N9: Part1.D4, J7.pulse
  N10: Part1.D5_PWM, J3.pulse
  N11: Part1.D6_PWM, J6.pulse
  N12: Part1.D7, J5.pulse
  N13: Part1.5V, SD_card_module1.+5
  VCC: Part1.VIN, J1.vcc, J3.vcc, J5.vcc, U1.+
  N14: M1.VO_(BLU), BAT1.V+

notes:
  Inductive proximity sensor
  base servo
  sholder servo
  elbow servo
  wrist servo
  hand servo
  gripper servo
  Micro SD card Module
  Circuit Layout

custom parts:
  LJ18A3-H-ZBX: LJ18A3-H-ZBX Proximity Sensor module.
  SD Card Module: SD Card Module Slot Socket Reader For Arduino ARM MCU
